# Fritzing sketch incubator (saved by Fritzing 0.9.2b)
perfboards: 1

parts:
  J1_Peltier = Peltier Element
  F1_Fan_12VDC = Fan - Ventilador [package=THT]
  12VDC_in = 2.1mm Barrel Jack with Terminal Block
  S2 = H-Bridge with L298N v2
  R16 = Resistor [tolerance=±5% resistance=4.7k package=THT]
  R17 = Resistor [tolerance=±5% resistance=2.0k package=THT]
  C16 = Electrolytic Capacitor [capacitance=10µF package="100 mil [THT, electrolytic]"]
  100k_Therm1 = Temperature Sensor (Thermistor) [thermistor_type=NTC package=THT]
  R19 = Resistor [tolerance=±5% resistance=4.7k package=THT]
  R20 = Resistor [tolerance=±5% resistance=2.0k package=THT]
  C17 = Electrolytic Capacitor [capacitance=10µF package="100 mil [THT, electrolytic]"]
  100k_Therm2 = Temperature Sensor (Thermistor) [thermistor_type=NTC package=THT]
  R22 = Resistor [tolerance=±5% resistance=4.7k package=THT]
  R23 = Resistor [tolerance=±5% resistance=2.0k package=THT]
  C19 = Electrolytic Capacitor [capacitance=10µF package="100 mil [THT, electrolytic]"]
  100k_Therm3 = Temperature Sensor (Thermistor) [thermistor_type=NTC package=THT]
  C23 = Ceramic Capacitor [capacitance=100nF voltage=20V package="100 mil [THT, multilayer]"]
  C24 = Ceramic Capacitor [capacitance=100nF package="100 mil [THT, multilayer]"]
  C25 = Ceramic Capacitor [capacitance=100nF package="100 mil [THT, multilayer]"]
  Part2 = IRF540 MOSFET module
  PocketBeagle = PocketBeagle

nets:
  N1: J1_Peltier.pin1, S2.OUT2, S2.OUT3
  N2: J1_Peltier.pin2, S2.OUT1, S2.OUT4
  N3: F1_Fan_12VDC.5V, Part2.Vout+
  N4: F1_Fan_12VDC.GND, Part2.Vout-
  N5: 12VDC_in.POS, S2.+VS, Part2.Vin+
  GND: 12VDC_in.NEG, S2.GND, Part2.V-, Part2.Vin-, PocketBeagle.GND
  N6: S2.+VSS, Part2.V+, PocketBeagle.VIN
  N7: S2.ENA, S2.ENB, PocketBeagle.GPIO59
  N8: S2.IN1, S2.IN4, PocketBeagle.GPIO58
  N9: S2.IN2, S2.IN3, PocketBeagle.GPIO57
  N10: R16.Pin_0, R17.Pin_0, 100k_Therm1.pin_1
  N11: R16.Pin_1, C16.+, C24.1, PocketBeagle.AIN0(1.8V)
  N12: R17.Pin_1, R20.Pin_1, R23.Pin_1, PocketBeagle.AIN.VREFP
  N13: C16.-, 100k_Therm1.pin_0, C17.-, 100k_Therm2.pin_0, C19.-, 100k_Therm3.pin_0, C23.0, C24.0, C25.0, PocketBeagle.AIN.VREFN
  N14: R19.Pin_0, R20.Pin_0, 100k_Therm2.pin_1
  N15: R19.Pin_1, C17.+, C23.1, PocketBeagle.AIN1(1.8V)
  N16: R22.Pin_0, R23.Pin_0, 100k_Therm3.pin_1
  N17: R22.Pin_1, C19.+, C25.1, PocketBeagle.AIN2(1.8V)
  N18: Part2.S, PocketBeagle.GPIO20

notes:
  Configure both L298N 2A bridges in parallel for 4A Peltier
  Only Therm1 in use; others for future expansion

custom parts:
  Fan - Ventilador: Ventilador de 2 pines, se encuentra comunmente en computadoras de escritorio
  H-Bridge with L298N v2: h-bridge
